# Fritzing sketch parts (saved by Fritzing 0.9.3b)

parts:
  U2 = NodeMCU V1.0
  SSD1306 = OLED 128x64 I2C Monochrome Display
  7_-_9V_1a = Power plug
  HID_Card_Reader = Header 4 [package=1x04-1mm-ra]
  SCT-013_Curent_Sensor = 3.5mm Audio Jack [package=audio-jack-3.5mm-smd]
  220V_AC_Relay1 = RELAY-SOLIDSTATE [package=relay-s108t02]
  Bell_Relay = RELAY [package=relay-jzc]
  Reset_Button = Round Pushbutton

nets:
  N1: U2.D1, SSD1306.SCK
  N2: U2.D2, SSD1306.SDA
  N3: U2.D3, Bell_Relay.COIL1
  GND: U2.GND, SSD1306.GND, 7_-_9V_1a.GND, HID_Card_Reader.4, SCT-013_Curent_Sensor.SLEEVE, 220V_AC_Relay1.-, Bell_Relay.MAIN, Reset_Button.leg0
  N4: U2.D5, HID_Card_Reader.2
  N5: U2.D6, HID_Card_Reader.1
  N6: U2.D7, 220V_AC_Relay1.+
  3V3: U2.3V3, SSD1306.VDD
  VIN: U2.Vin, 7_-_9V_1a.VCC, HID_Card_Reader.3
  N7: U2.RST, Reset_Button.leg1
  N8: U2.A0, SCT-013_Curent_Sensor.RIGHT

custom parts:
  NodeMCU V1.0: ESP8266 based NodeMCU
